# Fritzing sketch Portdiagram (saved by Fritzing 0.9.3b)
circuit board: 8.46667cm x 5.64444cm

parts:
  SCL = rounded female pin header, 6 pins [form="♀ (female rounded)"]
  SDA = rounded female pin header, 6 pins [form="♀ (female rounded)"]
  GND = rounded female pin header, 6 pins [form="♀ (female rounded)"]
  VCC = rounded female pin header, 6 pins [form="♀ (female rounded)"]

nets:
  N1: SCL.pin1, SCL.pin2, SCL.pin3, SCL.pin4, SCL.pin5, SCL.pin6
  N2: SDA.pin1, SDA.pin2, SDA.pin3, SDA.pin4, SDA.pin5, SDA.pin6
  N3: GND.pin1, GND.pin2, GND.pin3, GND.pin4, GND.pin5, GND.pin6
  N4: VCC.pin1, VCC.pin2, VCC.pin3, VCC.pin4, VCC.pin5, VCC.pin6
