# Fritzing sketch ir array (saved by Fritzing 0.9.3b)
circuit board: 22.53cm x 13.73cm

parts:
  I/O = MCP23017 I2C I/O Expander
  IR1 = LED - 3mm [color="Red (633nm)" package="3 mm [THT]"]
  IR2 = LED - 3mm [color="Red (633nm)" package="3 mm [THT]"]
  IR3 = LED - 3mm [color="Red (633nm)" package="3 mm [THT]"]
  IR4 = LED - 3mm [color="Red (633nm)" package="3 mm [THT]"]
  IR5 = LED - 3mm [color="Red (633nm)" package="3 mm [THT]"]
  IR6 = LED - 3mm [color="Red (633nm)" package="3 mm [THT]"]
  IR7 = LED - 3mm [color="Red (633nm)" package="3 mm [THT]"]
  IR8 = LED - 3mm [color="Red (633nm)" package="3 mm [THT]"]
  IR9 = LED - 3mm [color="Red (633nm)" package="3 mm [THT]"]
  IR10 = LED - 3mm [color="Red (633nm)" package="3 mm [THT]"]
  IR11 = LED - 3mm [color="Red (633nm)" package="3 mm [THT]"]
  IR12 = LED - 3mm [color="Red (633nm)" package="3 mm [THT]"]
  IR13 = LED - 3mm [color="Red (633nm)" package="3 mm [THT]"]
  IR14 = LED - 3mm [color="Red (633nm)" package="3 mm [THT]"]
  IR15 = LED - 3mm [color="Red (633nm)" package="3 mm [THT]"]
  IR16 = LED - 3mm [color="Red (633nm)" package="3 mm [THT]"]
  Part1 = Arduino Nano (Rev3.0)  # not connected
  JP1 = Header 6 [package=1x06-smd]
  JP2 = Header 6 [package=1x06-smd]

nets:
  N1: I/O.GPB0, IR7.anode
  N2: I/O.GPB1, IR8.anode
  N3: I/O.GPB2, IR13.anode
  N4: I/O.GPB3, IR1.cathode, IR1.anode, IR2.cathode, IR3.cathode, IR4.cathode, IR5.cathode, IR6.cathode, IR7.cathode, IR8.cathode, IR9.cathode, IR10.cathode, IR11.cathode, IR12.cathode, IR13.cathode, IR14.cathode, IR15.cathode, IR16.cathode
  N5: I/O.GPB4, IR5.anode
  N6: I/O.GPB5, IR3.anode
  N7: I/O.GPB6, IR14.anode
  N8: I/O.GPB7, IR10.anode
  N9: I/O.VDD, JP2.6
  N10: I/O.VSS, JP2.5
  N11: I/O.NC#11, JP2.4
  N12: I/O.SCL, JP2.3
  N13: I/O.SDA, JP2.2
  N14: I/O.NC#14, JP2.1
  N15: I/O.A0, JP1.6
  N16: I/O.A1, JP1.5
  N17: I/O.A2, JP1.4
  N18: I/O.RESET, JP1.3
  N19: I/O.INTB, JP1.2
  N20: I/O.INTA, JP1.1
  N21: I/O.GPA0, IR12.anode
  N22: I/O.GPA1, IR11.anode
  N23: I/O.GPA2, IR16.anode
  N24: I/O.GPA3, IR2.anode
  N25: I/O.GPA4, IR6.anode
  N26: I/O.GPA5, IR4.anode
  N27: I/O.GPA6, IR15.anode
  N28: I/O.GPA7, IR9.anode

custom parts:
  MCP23017 I2C I/O Expander: The MCP23017 uses two i2c pins (these can be shared with other i2c devices), and in exchange gives you 16 general purpose pins. You can set each of 16 pins to be input, output, input with a pullup or open drain. There's even the ability to get an interrupt via an external pin when any of the inputs change so you don't have to keep polling the chip.
